# Fritzing sketch schematic (saved by Fritzing 0.9.2b)
breadboards: 1

parts:
  Raspberry_Pi1 = Raspberry Pi B rev2
  LED1 = LED - 5mm [color="Red (633nm)" package="5 mm [THT]"]
  R1 = Resistor [tolerance=±5% resistance=220 package="2010 [SMD]"]
  DHT1 = DHT11 Humitidy and Temperature Sensor
  R2 = Resistor [tolerance=±5% resistance=220 package="2010 [SMD]"]

nets:
  3V3: Raspberry_Pi1.3V3, DHT1.VDD, R2.Pin_0
  GND: Raspberry_Pi1.GND, LED1.cathode, DHT1.GND
  N1: Raspberry_Pi1.GPIO_14, R1.Pin_1
  N2: Raspberry_Pi1.GPIO_4, DHT1.NULL
  N3: LED1.anode, R1.Pin_0
  N4: DHT1.DATA, R2.Pin_1

custom parts:
  DHT11 Humitidy and Temperature Sensor: DHT11 Humidity and Temperature Sensor
